# Fritzing sketch completo (saved by Fritzing 0.9.3b)
breadboards: 2

parts:
  U1 = ESP8266 NodeMCU LoLin module
  KY-1 = Keyes Relay [package=THT]
  VCC1 = Battery
  Part2 = HC-SR501 Body Sensor Module
  LED2 = LED - 5mm [color="Red (633nm)" package="5 mm [THT]"]

nets:
  N1: U1.D2, Part2.OUT
  3V3: U1.3V3, Part2.VCC
  GND: U1.GND, KY-1.ground, VCC1.-, Part2.GND, LED2.cathode
  N2: U1.D6, LED2.anode
  N3: U1.D8, KY-1.signal
  N4: U1.Vin, KY-1.power, VCC1.+

notes:
  OUT
  GND
  VCC

custom parts:
  ESP8266 NodeMCU LoLin module: ESP8266 based NodeMCU
  Keyes Relay: The Keyes 5V relay module is suitable for SCM development, home appliance control. It uses a 5V~12V TIL control signal which can control DC / AC signal.
  HC-SR501 Body Sensor Module: Pyroelectric Infrared PIR Motion Sensor Detector Module
