# Fritzing sketch desafio1 (saved by Fritzing 0.9.3b)
breadboards: 2

parts:
  U1 = ESP8266 NodeMCU LoLin module
  LED1 = LED - 5mm [color="Red (633nm)" package="5 mm [THT]"]
  LED2 = LED - 5mm [color="Red (633nm)" package="5 mm [THT]"]  # not connected

nets:
  N1: U1.GND, LED1.cathode
  N2: U1.D8, LED1.anode

notes:
  Positivo (+)
  Negativo (-)

custom parts:
  ESP8266 NodeMCU LoLin module: ESP8266 based NodeMCU
