# Fritzing sketch desafio4 (saved by Fritzing 0.9.3b)
breadboards: 2

parts:
  U1 = ESP8266 NodeMCU LoLin module
  Part2 = HC-SR501 Body Sensor Module
  LED2 = LED - 5mm [color="Red (633nm)" package="5 mm [THT]"]
  LED3 = LED - 5mm [color="Yellow (585nm)" package="5 mm [THT]"]

nets:
  N1: U1.D2, Part2.OUT
  3V3: U1.3V3, Part2.VCC
  GND: U1.GND, Part2.GND, LED3.cathode
  N2: U1.D6, LED3.anode
  N3: U1.D8, LED2.anode
  N4: U1.TX, LED2.cathode

notes:
  OUT
  GND
  VCC

custom parts:
  ESP8266 NodeMCU LoLin module: ESP8266 based NodeMCU
  HC-SR501 Body Sensor Module: Pyroelectric Infrared PIR Motion Sensor Detector Module
