# Fritzing sketch desafio5 (saved by Fritzing 0.9.3b)
breadboards: 2

parts:
  U1 = ESP8266 NodeMCU LoLin module
  LED1 = LED - 5mm [color="Red (633nm)" package="5 mm [THT]"]
  Part1 = HC-SR501 Body Sensor Module
  KY-1 = Keyes Relay [package=THT]

nets:
  N1: U1.D2, Part1.OUT
  3V3: U1.3V3, Part1.VCC
  GND: U1.GND, LED1.cathode, Part1.GND, KY-1.ground
  N2: U1.D6, LED1.anode
  N3: U1.D8, KY-1.signal
  N4: U1.Vin, KY-1.power

notes:
  VCC
  GND
  OUT

custom parts:
  ESP8266 NodeMCU LoLin module: ESP8266 based NodeMCU
  HC-SR501 Body Sensor Module: Pyroelectric Infrared PIR Motion Sensor Detector Module
  Keyes Relay: The Keyes 5V relay module is suitable for SCM development, home appliance control. It uses a 5V~12V TIL control signal which can control DC / AC signal.
